// Logisim project SAP1-Arq1-FinalL.circ as structural Verilog
// EP
module main (
  input  Reset
);

  wire CLK, Clock_out, CLR, Cp, Ea, Ep, Eu, nCE, nCLK, nCLR, nEi, nLa, nLb, nLi, nLm, nLo, not_1_out,
       \registrador_intruções_1_x4 , \registrador_intruções_1_x5 , \registrador_intruções_1_x6 ,
       \registrador_intruções_1_x7 , Su;
  wire [3:0] rem_1_out, rs_1_out, rs_1_out_2;
  wire [7:0] acumulador_1_out_somador, registrador_b_1_out, W;

  REM rem_1 (.Out(rem_1_out), .CLK(CLK), .Lm(nLm), .in_3(W));
  not not_1 (not_1_out, nCE);
  Clock Clock (.out(Clock_out));
  Contador_Programa contador_programa_1 (.Cp(Cp), .CLR(nCLR), .CLK(nCLK), .Out(W), .Ep(Ep));
  RAM #(.addrWidth(4)) ram_1 (.addr(rem_1_out), .data(W), .sel(not_1_out), .clk(CLK), .ld(not_1_out));  // open: clr
  \Registrador_Intruções  \registrador_intruções_1  (
    .In(W), .Out(W), .Ei(nEi), .X7(\registrador_intruções_1_x7 ), .X6(\registrador_intruções_1_x6 ),
    .X5(\registrador_intruções_1_x5 ), .X4(\registrador_intruções_1_x4 ), .CLK(CLK), .Li(nLi), .CLR(CLR));
  Acumulador acumulador_1 (.Out(W), .Out_somador(acumulador_1_out_somador), .CLK(CLK), .La(nLa), .Ea(Ea), .In(W));
  RS rs_1 (.Out({rs_1_out_2, rs_1_out}), .CLK(CLK), .nLa(nLo), .CLR(CLR), .In(W));
  Hex_Digit_Display hex_digit_display_1 (.value(rs_1_out_2));  // open: dp
  Somador_Subtrator somador_subtrator_1 (
    .B(registrador_b_1_out), .A(acumulador_1_out_somador), .Eu(Eu), .Su(Su), .out_5(W));
  Registrador_B registrador_b_1 (.In(W), .Out(registrador_b_1_out), .Lb(nLb), .CLK(CLK));
  Hex_Digit_Display hex_digit_display_2 (.value(rs_1_out));  // open: dp
  Controlador_Sequenciador controlador_sequenciador_1 (
    .CLR_CPU(Reset), .CLK_CPU(Clock_out), .X7(\registrador_intruções_1_x7 ), .nCLR(nCLR), .CLR(CLR),
    .CLK(CLK), .nCLK(nCLK), .Cp(Cp), .Ep(Ep), .nLm(nLm), .nCE(nCE), .nL1(nLi), .nE1(nEi), .nLa(nLa), .Ea(Ea),
    .Su(Su), .Eu(Eu), .nLb(nLb), .nLo(nLo), .X6(\registrador_intruções_1_x6 ),
    .X5(\registrador_intruções_1_x5 ), .X4(\registrador_intruções_1_x4 ));

  // Notes on the sheet:
  //   LDA 0
  //   ADD 1
  //   SUB 2
  //   OUT e
  //   HLT f
  //   S
  //   A
  //   P
  //   1
endmodule

module Contador_Programa (
  input  Cp,
  input  CLK,
  input  CLR,
  input  Ep,
  output [7:0] Out
);

  wire j_k_ff_1_qn, j_k_ff_2_qn, j_k_ff_3_qn, j_k_ff_4_qn, j_k_ff_5_qn, j_k_ff_6_qn, j_k_ff_7_qn, not_1_out;
  wire [7:0] j_k_ff_1_q;

  not not_1 (not_1_out, CLR);
  J_K_Flip_Flop j_k_ff_1 (
    .J(Cp), .clk(CLK), .K(Cp), .Q(j_k_ff_1_q[0]), .Qn(j_k_ff_1_qn), .en(Cp), .reset(not_1_out));  // open: preset
  assign Out = Ep ? j_k_ff_1_q : 8'bz;  // Controlled_Buffer controlled_buffer_1
  J_K_Flip_Flop j_k_ff_2 (
    .J(Cp), .clk(j_k_ff_1_qn), .K(Cp), .Q(j_k_ff_1_q[1]), .Qn(j_k_ff_2_qn), .en(Cp), .reset(not_1_out));  // open: preset
  J_K_Flip_Flop j_k_ff_3 (
    .J(Cp), .clk(j_k_ff_2_qn), .K(Cp), .Q(j_k_ff_1_q[2]), .Qn(j_k_ff_3_qn), .en(Cp), .reset(not_1_out));  // open: preset
  J_K_Flip_Flop j_k_ff_4 (
    .J(Cp), .clk(j_k_ff_3_qn), .K(Cp), .Q(j_k_ff_1_q[3]), .Qn(j_k_ff_4_qn), .en(Cp), .reset(not_1_out));  // open: preset
  J_K_Flip_Flop j_k_ff_5 (
    .J(Cp), .clk(j_k_ff_4_qn), .K(Cp), .Q(j_k_ff_1_q[4]), .Qn(j_k_ff_5_qn), .en(Cp), .reset(not_1_out));  // open: preset
  J_K_Flip_Flop j_k_ff_6 (
    .J(Cp), .clk(j_k_ff_5_qn), .K(Cp), .Q(j_k_ff_1_q[5]), .Qn(j_k_ff_6_qn), .en(Cp), .reset(not_1_out));  // open: preset
  J_K_Flip_Flop j_k_ff_7 (
    .J(Cp), .clk(j_k_ff_6_qn), .K(Cp), .Q(j_k_ff_1_q[6]), .Qn(j_k_ff_7_qn), .en(Cp), .reset(not_1_out));  // open: preset
  J_K_Flip_Flop j_k_ff_8 (
    .J(Cp), .clk(j_k_ff_7_qn), .K(Cp), .Q(j_k_ff_1_q[7]), .en(Cp), .reset(not_1_out));  // open: Qn, preset

  // Notes on the sheet:
  //   Foi escolhido o jk pela condição de toggle
endmodule

module \Registrador_Intruções  (
  input  Ei,
  input  CLK,
  input  Li,
  input  CLR,
  input  [7:0] In,
  output [7:0] Out,
  output X7,
  output X6,
  output X5,
  output X4
);

  wire d_ff_5_q, d_ff_6_q, d_ff_7_q, d_ff_8_q, not_1_out, not_2_out;

  not not_1 (not_1_out, Ei);
  D_Flip_Flop d_ff_1 (.clk(CLK), .D(In[7]), .Q(X7), .en(not_2_out), .reset(CLR));  // open: Qn, preset
  not not_2 (not_2_out, Li);
  D_Flip_Flop d_ff_2 (.clk(CLK), .D(In[6]), .Q(X6), .en(not_2_out), .reset(CLR));  // open: Qn, preset
  assign Out[7] = not_1_out ? 1'b0 : 1'bz;  // Controlled_Buffer controlled_buffer_1
  D_Flip_Flop d_ff_3 (.clk(CLK), .D(In[5]), .Q(X5), .en(not_2_out), .reset(CLR));  // open: Qn, preset
  D_Flip_Flop d_ff_4 (.clk(CLK), .D(In[4]), .Q(X4), .en(not_2_out), .reset(CLR));  // open: Qn, preset
  assign Out[3] = not_1_out ? d_ff_5_q : 1'bz;  // Controlled_Buffer controlled_buffer_2
  D_Flip_Flop d_ff_5 (.clk(CLK), .D(In[3]), .Q(d_ff_5_q), .en(not_2_out), .reset(CLR));  // open: Qn, preset
  assign Out[2] = not_1_out ? d_ff_6_q : 1'bz;  // Controlled_Buffer controlled_buffer_3
  D_Flip_Flop d_ff_6 (.clk(CLK), .D(In[2]), .Q(d_ff_6_q), .en(not_2_out), .reset(CLR));  // open: Qn, preset
  assign Out[1] = not_1_out ? d_ff_7_q : 1'bz;  // Controlled_Buffer controlled_buffer_4
  D_Flip_Flop d_ff_7 (.clk(CLK), .D(In[1]), .Q(d_ff_7_q), .en(not_2_out), .reset(CLR));  // open: Qn, preset
  assign Out[0] = not_1_out ? d_ff_8_q : 1'bz;  // Controlled_Buffer controlled_buffer_5
  D_Flip_Flop d_ff_8 (.clk(CLK), .D(In[0]), .Q(d_ff_8_q), .en(not_2_out), .reset(CLR));  // open: Qn, preset

  assign Out[6:4] = {3{Out[7]}};
endmodule

module REM (
  input  CLK,
  input  Lm,
  input  [7:0] in_3,
  output [3:0] Out
);

  wire not_1_out;

  not not_1 (not_1_out, Lm);
  D_Flip_Flop d_ff_1 (.clk(CLK), .D(in_3[3]), .Q(Out[3]), .en(not_1_out));  // open: Qn, preset, reset
  D_Flip_Flop d_ff_2 (.clk(CLK), .D(in_3[2]), .Q(Out[2]), .en(not_1_out));  // open: Qn, preset, reset
  D_Flip_Flop d_ff_3 (.clk(CLK), .D(in_3[1]), .Q(Out[1]), .en(not_1_out));  // open: Qn, preset, reset
  D_Flip_Flop d_ff_4 (.clk(CLK), .D(in_3[0]), .Q(Out[0]), .en(not_1_out));  // open: Qn, preset, reset

  assign in_3[6:4] = {3{in_3[7]}};
  // also tied to GND on the sheet: in_3[7]

  // Notes on the sheet:
  //   Registra apenas os 4 btis menos significativos
endmodule

module Acumulador (
  input  CLK,
  input  La,
  input  Ea,
  input  [7:0] In,
  output [7:0] Out,
  output [7:0] Out_somador
);

  wire not_1_out;

  not not_1 (not_1_out, La);
  assign Out[7] = Ea ? Out_somador[7] : 1'bz;  // Controlled_Buffer controlled_buffer_1
  D_Flip_Flop d_ff_1 (.clk(CLK), .D(In[7]), .Q(Out_somador[7]), .en(not_1_out));  // open: Qn, preset, reset
  assign Out[6] = Ea ? Out_somador[6] : 1'bz;  // Controlled_Buffer controlled_buffer_2
  D_Flip_Flop d_ff_2 (.clk(CLK), .D(In[6]), .Q(Out_somador[6]), .en(not_1_out));  // open: Qn, preset, reset
  assign Out[5] = Ea ? Out_somador[5] : 1'bz;  // Controlled_Buffer controlled_buffer_3
  D_Flip_Flop d_ff_3 (.clk(CLK), .D(In[5]), .Q(Out_somador[5]), .en(not_1_out));  // open: Qn, preset, reset
  assign Out[4] = Ea ? Out_somador[4] : 1'bz;  // Controlled_Buffer controlled_buffer_4
  D_Flip_Flop d_ff_4 (.clk(CLK), .D(In[4]), .Q(Out_somador[4]), .en(not_1_out));  // open: Qn, preset, reset
  assign Out[3] = Ea ? Out_somador[3] : 1'bz;  // Controlled_Buffer controlled_buffer_5
  D_Flip_Flop d_ff_5 (.clk(CLK), .D(In[3]), .Q(Out_somador[3]), .en(not_1_out));  // open: Qn, preset, reset
  assign Out[2] = Ea ? Out_somador[2] : 1'bz;  // Controlled_Buffer controlled_buffer_6
  D_Flip_Flop d_ff_6 (.clk(CLK), .D(In[2]), .Q(Out_somador[2]), .en(not_1_out));  // open: Qn, preset, reset
  assign Out[1] = Ea ? Out_somador[1] : 1'bz;  // Controlled_Buffer controlled_buffer_7
  D_Flip_Flop d_ff_7 (.clk(CLK), .D(In[1]), .Q(Out_somador[1]), .en(not_1_out));  // open: Qn, preset, reset
  assign Out[0] = Ea ? Out_somador[0] : 1'bz;  // Controlled_Buffer controlled_buffer_8
  D_Flip_Flop d_ff_8 (.clk(CLK), .D(In[0]), .Q(Out_somador[0]), .en(not_1_out));  // open: Qn, preset, reset
endmodule

module Registrador_B (
  input  CLK,
  input  Lb,
  input  [7:0] In,
  output [7:0] Out
);

  wire not_1_out;

  not not_1 (not_1_out, Lb);
  D_Flip_Flop d_ff_1 (.clk(CLK), .D(In[7]), .Q(Out[7]), .en(not_1_out));  // open: Qn, preset, reset
  D_Flip_Flop d_ff_2 (.clk(CLK), .D(In[6]), .Q(Out[6]), .en(not_1_out));  // open: Qn, preset, reset
  D_Flip_Flop d_ff_3 (.clk(CLK), .D(In[5]), .Q(Out[5]), .en(not_1_out));  // open: Qn, preset, reset
  D_Flip_Flop d_ff_4 (.clk(CLK), .D(In[4]), .Q(Out[4]), .en(not_1_out));  // open: Qn, preset, reset
  D_Flip_Flop d_ff_5 (.clk(CLK), .D(In[3]), .Q(Out[3]), .en(not_1_out));  // open: Qn, preset, reset
  D_Flip_Flop d_ff_6 (.clk(CLK), .D(In[2]), .Q(Out[2]), .en(not_1_out));  // open: Qn, preset, reset
  D_Flip_Flop d_ff_7 (.clk(CLK), .D(In[1]), .Q(Out[1]), .en(not_1_out));  // open: Qn, preset, reset
  D_Flip_Flop d_ff_8 (.clk(CLK), .D(In[0]), .Q(Out[0]), .en(not_1_out));  // open: Qn, preset, reset
endmodule

module RS (
  input  CLK,
  input  nLa,
  input  CLR,
  input  [7:0] In,
  output [7:0] Out
);

  wire not_1_out;

  not not_1 (not_1_out, nLa);
  D_Flip_Flop d_ff_1 (.clk(CLK), .D(In[7]), .Q(Out[7]), .en(not_1_out), .reset(CLR));  // open: Qn, preset
  D_Flip_Flop d_ff_2 (.clk(CLK), .D(In[6]), .Q(Out[6]), .en(not_1_out), .reset(CLR));  // open: Qn, preset
  D_Flip_Flop d_ff_3 (.clk(CLK), .D(In[5]), .Q(Out[5]), .en(not_1_out), .reset(CLR));  // open: Qn, preset
  D_Flip_Flop d_ff_4 (.clk(CLK), .D(In[4]), .Q(Out[4]), .en(not_1_out), .reset(CLR));  // open: Qn, preset
  D_Flip_Flop d_ff_5 (.clk(CLK), .D(In[3]), .Q(Out[3]), .en(not_1_out), .reset(CLR));  // open: Qn, preset
  D_Flip_Flop d_ff_6 (.clk(CLK), .D(In[2]), .Q(Out[2]), .en(not_1_out), .reset(CLR));  // open: Qn, preset
  D_Flip_Flop d_ff_7 (.clk(CLK), .D(In[1]), .Q(Out[1]), .en(not_1_out), .reset(CLR));  // open: Qn, preset
  D_Flip_Flop d_ff_8 (.clk(CLK), .D(In[0]), .Q(Out[0]), .en(not_1_out), .reset(CLR));  // open: Qn, preset
endmodule

module somador_completo (
  input  A,
  input  B,
  input  VEM_1,
  output VAI_1,
  output soma
);

  wire and_1_out, and_2_out, and_3_out, xor_1_out;

  and and_1 (and_1_out, A, B);
  and and_2 (and_2_out, A, VEM_1);
  and and_3 (and_3_out, B, VEM_1);
  xor xor_1 (xor_1_out, A, B);
  or or_1 (VAI_1, and_1_out, and_2_out, and_3_out);
  xor xor_2 (soma, xor_1_out, VEM_1);
endmodule

module meio_somador (
  input  A,
  input  VEM_1,
  output VAI_UM,
  output SOMA
);

  and and_1 (VAI_UM, VEM_1, A);
  xor xor_1 (SOMA, VEM_1, A);
endmodule

module complemento_1 (
  input  A7,
  input  A6,
  input  A5,
  input  A4,
  input  A3,
  input  A2,
  input  A1,
  input  A0,
  input  in_9,
  output R7,
  output R6,
  output R5,
  output R4,
  output out_14,
  output R2,
  output R1,
  output R0
);

  xor xor_1 (R7, A7, in_9);
  xor xor_2 (R6, A6, in_9);
  xor xor_3 (R5, A5, in_9);
  xor xor_4 (R4, A4, in_9);
  xor xor_5 (out_14, A3, in_9);
  xor xor_6 (R2, A2, in_9);
  xor xor_7 (R1, A1, in_9);
  xor xor_8 (R0, A0, in_9);
endmodule

// complemeto 2
module complemento_2 (
  input  A7,
  input  A6,
  input  A5,
  input  A4,
  input  A3,
  input  A2,
  input  A1,
  input  A0,
  input  in_9,
  output out_10,
  output out_11,
  output out_12,
  output out_13,
  output out_14,
  output out_15,
  output out_16,
  output out_17
);

  wire meio_somador_1_vai_um, meio_somador_2_vai_um, meio_somador_3_vai_um, meio_somador_4_vai_um,
       meio_somador_5_vai_um, meio_somador_6_vai_um, meio_somador_7_vai_um, meio_somador_8_vai_um;

  meio_somador meio_somador_1 (.VAI_UM(meio_somador_1_vai_um), .A(A7), .VEM_1(meio_somador_2_vai_um), .SOMA(out_10));
  LED led_1 (.in(meio_somador_1_vai_um));
  meio_somador meio_somador_2 (.VAI_UM(meio_somador_2_vai_um), .A(A6), .VEM_1(meio_somador_4_vai_um), .SOMA(out_11));
  meio_somador meio_somador_3 (.VAI_UM(meio_somador_3_vai_um), .A(A4), .VEM_1(meio_somador_5_vai_um), .SOMA(out_13));
  meio_somador meio_somador_4 (.VAI_UM(meio_somador_4_vai_um), .A(A5), .VEM_1(meio_somador_3_vai_um), .SOMA(out_12));
  meio_somador meio_somador_5 (.VAI_UM(meio_somador_5_vai_um), .A(A3), .VEM_1(meio_somador_6_vai_um), .SOMA(out_14));
  meio_somador meio_somador_6 (.VAI_UM(meio_somador_6_vai_um), .A(A2), .VEM_1(meio_somador_7_vai_um), .SOMA(out_15));
  meio_somador meio_somador_7 (.VAI_UM(meio_somador_7_vai_um), .A(A1), .VEM_1(meio_somador_8_vai_um), .SOMA(out_16));
  meio_somador meio_somador_8 (.VAI_UM(meio_somador_8_vai_um), .A(A0), .VEM_1(in_9), .SOMA(out_17));
endmodule

module Somador_Subtrator (
  input  [7:0] B,
  input  Su,
  input  [7:0] A,
  input  Eu,
  output [7:0] out_5
);

  wire complemento_1_1_out_14, complemento_1_1_r0, complemento_1_1_r1, complemento_1_1_r2,
       complemento_1_1_r4, complemento_1_1_r5, complemento_1_1_r6, complemento_1_1_r7,
       complemento_2_1_out_10, complemento_2_1_out_11, complemento_2_1_out_12, complemento_2_1_out_13,
       complemento_2_1_out_14, complemento_2_1_out_15, complemento_2_1_out_16, complemento_2_1_out_17,
       somador_4bits_1_out_11, somador_4bits_1_out_12, somador_4bits_1_out_14, somador_4bits_1_resultado,
       somador_4bits_1_vai_1, somador_4bits_2_out_11, somador_4bits_2_out_12, somador_4bits_2_out_14,
       somador_4bits_2_resultado, somador_4bits_2_vai_1;

  LED led_1 (.in(somador_4bits_1_vai_1));
  somador_4bits somador_4bits_1 (
    .vai_1(somador_4bits_1_vai_1), .in_1(A[7]), .Variavel_A(A[6]), .in_3(A[5]), .in_4(A[4]),
    .in_5(complemento_2_1_out_10), .Variavel_B(complemento_2_1_out_11), .in_7(complemento_2_1_out_12),
    .in_8(complemento_2_1_out_13), .vem1(somador_4bits_2_vai_1), .out_11(somador_4bits_1_out_11),
    .out_12(somador_4bits_1_out_12), .Resultado(somador_4bits_1_resultado), .out_14(somador_4bits_1_out_14));
  assign out_5[5] = Eu ? somador_4bits_1_resultado : 1'bz;  // Controlled_Buffer controlled_buffer_1
  assign out_5[6] = Eu ? somador_4bits_1_out_12 : 1'bz;  // Controlled_Buffer controlled_buffer_2
  assign out_5[7] = Eu ? somador_4bits_1_out_11 : 1'bz;  // Controlled_Buffer controlled_buffer_3
  somador_4bits somador_4bits_2 (
    .vai_1(somador_4bits_2_vai_1), .in_1(A[3]), .Variavel_A(A[2]), .in_3(A[1]), .in_4(A[0]),
    .in_5(complemento_2_1_out_14), .Variavel_B(complemento_2_1_out_15), .in_7(complemento_2_1_out_16),
    .in_8(complemento_2_1_out_17), .vem1(1'b0), .out_11(somador_4bits_2_out_11),
    .out_12(somador_4bits_2_out_12), .Resultado(somador_4bits_2_resultado), .out_14(somador_4bits_2_out_14));
  assign out_5[1] = Eu ? somador_4bits_2_resultado : 1'bz;  // Controlled_Buffer controlled_buffer_4
  assign out_5[2] = Eu ? somador_4bits_2_out_12 : 1'bz;  // Controlled_Buffer controlled_buffer_5
  assign out_5[3] = Eu ? somador_4bits_2_out_11 : 1'bz;  // Controlled_Buffer controlled_buffer_6
  assign out_5[4] = Eu ? somador_4bits_1_out_14 : 1'bz;  // Controlled_Buffer controlled_buffer_7
  assign out_5[0] = Eu ? somador_4bits_2_out_14 : 1'bz;  // Controlled_Buffer controlled_buffer_8
  complemento_1 complemento_1_1 (
    .A7(B[7]), .A6(B[6]), .A5(B[5]), .A4(B[4]), .A3(B[3]), .A2(B[2]), .A1(B[1]), .A0(B[0]),
    .R7(complemento_1_1_r7), .R6(complemento_1_1_r6), .R5(complemento_1_1_r5), .R4(complemento_1_1_r4),
    .out_14(complemento_1_1_out_14), .R2(complemento_1_1_r2), .R1(complemento_1_1_r1),
    .R0(complemento_1_1_r0), .in_9(Su));
  complemento_2 complemento_2_1 (
    .A7(complemento_1_1_r7), .A6(complemento_1_1_r6), .A5(complemento_1_1_r5), .A4(complemento_1_1_r4),
    .A3(complemento_1_1_out_14), .A2(complemento_1_1_r2), .A1(complemento_1_1_r1), .A0(complemento_1_1_r0),
    .out_10(complemento_2_1_out_10), .out_11(complemento_2_1_out_11), .out_12(complemento_2_1_out_12),
    .out_13(complemento_2_1_out_13), .out_14(complemento_2_1_out_14), .out_15(complemento_2_1_out_15),
    .out_16(complemento_2_1_out_16), .out_17(complemento_2_1_out_17), .in_9(Su));
endmodule

// somador 4b
module somador_4bits (
  input  in_1,
  input  Variavel_A,
  input  in_3,
  input  in_4,
  input  in_5,
  input  Variavel_B,
  input  in_7,
  input  in_8,
  input  vem1,
  output vai_1,
  output out_11,
  output out_12,
  output Resultado,
  output out_14
);

  wire somador_completo_2_vai_1, somador_completo_3_vai_1, somador_completo_4_vai_1;

  somador_completo somador_completo_1 (
    .VAI_1(vai_1), .A(in_1), .B(in_5), .VEM_1(somador_completo_2_vai_1), .soma(out_11));
  somador_completo somador_completo_2 (
    .VAI_1(somador_completo_2_vai_1), .A(Variavel_A), .B(Variavel_B), .VEM_1(somador_completo_3_vai_1),
    .soma(out_12));
  somador_completo somador_completo_3 (
    .VAI_1(somador_completo_3_vai_1), .A(in_3), .B(in_7), .VEM_1(somador_completo_4_vai_1), .soma(Resultado));
  somador_completo somador_completo_4 (
    .VAI_1(somador_completo_4_vai_1), .A(in_4), .B(in_8), .VEM_1(vem1), .soma(out_14));

  // Notes on the sheet:
  //   Estouro
  //   SOMADOR DE 4bits
endmodule

module Controlador_Sequenciador (
  input  CLR_CPU,
  input  CLK_CPU,
  input  X7,
  input  X6,
  input  X5,
  input  X4,
  output nCLR,
  output CLR,
  output CLK,
  output nCLK,
  output Cp,
  output Ep,
  output nLm,
  output nCE,
  output nL1,
  output nE1,
  output nLa,
  output Ea,
  output Su,
  output Eu,
  output nLb,
  output nLo
);

  wire ADD, HLT, j_k_ff_1_q, j_k_ff_2_qn, j_k_ff_3_qn, j_k_ff_4_qn, j_k_ff_5_qn, j_k_ff_6_qn, LDA,
       nand_1_out, nand_2_out, nand_3_out, nand_4_out, nand_5_out, nand_6_out, nand_7_out, nand_8_out,
       nand_9_out, nand_10_out, nand_11_out, nand_12_out, nand_13_out, nand_14_out, nand_15_out, nand_16_out,
       nand_17_out, nand_18_out, not_1_out, not_2_out, not_3_out, not_4_out, not_5_out, not_8_out, not_9_out,
       not_10_out, not_11_out, not_12_out, not_14_out, not_15_out, not_16_out, not_17_out, not_19_out,
       not_21_out, not_22_out, not_23_out, not_25_out, not_26_out, not_27_out, not_31_out, not_32_out,
       not_33_out, not_34_out, or_1_out, or_2_out, or_3_out, or_4_out, or_6_out, OUT, SUB, T3, T4, T5, T6;

  not not_1 (not_1_out, X7);
  not not_2 (not_2_out, X6);
  not not_3 (not_3_out, X5);
  not not_4 (not_4_out, HLT);
  not not_5 (not_5_out, X4);
  and and_1 (CLK, not_4_out, CLK_CPU);
  and and_2 (LDA, not_1_out, not_2_out, not_3_out, not_5_out);
  and and_3 (ADD, not_1_out, not_2_out, not_3_out, X4);
  and and_4 (SUB, not_1_out, not_2_out, X5, not_5_out);
  and and_5 (OUT, X7, X6, X5, not_5_out);
  and and_6 (HLT, X7, X6, X5, X4);
  not not_6 (nCLR, CLR_CPU);
  not not_7 (nCLK, CLK);
  J_K_Flip_Flop j_k_ff_1 (
    .J(j_k_ff_6_qn), .clk(CLK), .K(T6), .Q(j_k_ff_1_q), .Qn(Ep), .reset(CLR_CPU));  // open: preset, en
  not not_8 (not_8_out, Ep);
  nand nand_1 (nand_1_out, LDA, T4);
  J_K_Flip_Flop j_k_ff_2 (
    .J(Ep), .clk(CLK), .K(j_k_ff_1_q), .Q(Cp), .Qn(j_k_ff_2_qn), .reset(CLR_CPU));  // open: preset, en
  nand nand_2 (nand_2_out, ADD, T4);
  not not_9 (not_9_out, nand_1_out);
  not not_10 (not_10_out, not_8_out);
  not not_11 (not_11_out, nand_3_out);
  not not_12 (not_12_out, nand_2_out);
  or or_1 (or_1_out, not_10_out, not_9_out, not_12_out, not_11_out);
  not not_13 (nLm, or_1_out);
  J_K_Flip_Flop j_k_ff_3 (
    .J(Cp), .clk(CLK), .K(j_k_ff_2_qn), .Q(T3), .Qn(j_k_ff_3_qn), .reset(CLR_CPU));  // open: preset, en
  nand nand_3 (nand_3_out, SUB, T4);
  not not_14 (not_14_out, T3);
  nand nand_4 (nand_4_out, LDA, T5);
  J_K_Flip_Flop j_k_ff_4 (
    .J(T3), .clk(CLK), .K(j_k_ff_3_qn), .Q(T4), .Qn(j_k_ff_4_qn), .reset(CLR_CPU));  // open: preset, en
  nand nand_5 (nand_5_out, ADD, T5);
  not not_15 (not_15_out, nand_5_out);
  not not_16 (not_16_out, not_14_out);
  not not_17 (not_17_out, nand_4_out);
  or or_2 (or_2_out, not_16_out, not_17_out, not_15_out, not_19_out);
  not not_18 (nCE, or_2_out);
  J_K_Flip_Flop j_k_ff_5 (
    .J(T4), .clk(CLK), .K(j_k_ff_4_qn), .Q(T5), .Qn(j_k_ff_5_qn), .reset(CLR_CPU));  // open: preset, en
  nand nand_6 (nand_6_out, SUB, T5);
  not not_19 (not_19_out, nand_6_out);
  not not_20 (nL1, T3);
  J_K_Flip_Flop j_k_ff_6 (
    .J(T5), .clk(CLK), .K(j_k_ff_5_qn), .Q(T6), .Qn(j_k_ff_6_qn), .reset(CLR_CPU));  // open: preset, en
  nand nand_7 (nand_7_out, LDA, T4);
  nand nand_8 (nand_8_out, ADD, T4);
  not not_21 (not_21_out, nand_7_out);
  not not_22 (not_22_out, nand_8_out);
  not not_23 (not_23_out, nand_9_out);
  or or_3 (or_3_out, not_21_out, not_22_out, not_23_out);
  not not_24 (nE1, or_3_out);
  nand nand_9 (nand_9_out, SUB, T4);
  nand nand_10 (nand_10_out, LDA, T5);
  not not_25 (not_25_out, nand_10_out);
  nand nand_11 (nand_11_out, ADD, T6);
  not not_26 (not_26_out, nand_11_out);
  not not_27 (not_27_out, nand_12_out);
  or or_4 (or_4_out, not_25_out, not_26_out, not_27_out);
  not not_28 (nLa, or_4_out);
  nand nand_12 (nand_12_out, SUB, T6);
  nand nand_13 (nand_13_out, OUT, T4);
  not not_29 (Ea, nand_13_out);
  nand nand_14 (nand_14_out, SUB, T6);
  not not_30 (Su, nand_14_out);
  nand nand_15 (nand_15_out, ADD, T6);
  not not_31 (not_31_out, nand_15_out);
  or or_5 (Eu, not_31_out, not_32_out);
  nand nand_16 (nand_16_out, SUB, T6);
  not not_32 (not_32_out, nand_16_out);
  nand nand_17 (nand_17_out, ADD, T5);
  not not_33 (not_33_out, nand_17_out);
  nand nand_18 (nand_18_out, SUB, T5);
  not not_34 (not_34_out, nand_18_out);
  or or_6 (or_6_out, not_33_out, not_34_out);
  not not_35 (nLb, or_6_out);
  nand nand_19 (nLo, T4, OUT);

  assign CLR = CLR_CPU;

  // Other names for the same wires on the sheet: T1 = Ep; T2 = Cp

  // Notes on the sheet:
  //   ENTRADA DO REGISTRADOR DE INSTRUÇÕES
  //   HTL SERVE PARA IMPDEDR A PASSAGEM DO CLOCK
  //   DEcodificador de instruçoes
  //   COMBINAÇÃO DE ESTADOS COM INSTRUÇOES
  //   Contador de anel
endmodule
